# Fritzing sketch kb2040_fightstick_v1.0 (saved by Fritzing 1.0.4)
circuit board: 5.01717cm x 6.68012cm
breadboards: 1

parts:
  KB2040 = Adafruit KB2040
  J1 = screw terminal, 10 pins
  J2 = screw terminal, 10 pins
  J3 = screw terminal, 10 pins
  J4 = screw terminal, 10 pins
  JOY = Adafruit Arcade Joystick
  S2_START = Arcade Button (yellow)
  S1_SEL = Arcade Button (green)
  L1 = Arcade Button (blue)
  R1 = Arcade Button (blue)
  L2 = Arcade Button (blue)
  R2 = Arcade Button (blue)
  OLED = OLED Monochrome 128x64 1.3 inch [part_number=938]
  Fn = Arcade Button (yellow)
  NeoPixel_DIN = NeoPixel Stick [part_number=1426]
  B4 = Arcade Button (blue)
  B2 = Arcade Button (blue)
  B3 = Arcade Button (blue)
  B1 = Arcade Button (blue)
  A2 = Arcade Button (red)
  A1_Home = Arcade Button (white)
  RESET = Pushbutton [package="[THT]"]
  USB = male pin header, 4 pins [form="♂ (male)"]

nets:
  GND: KB2040.GND, J1.pin1, J1.pin4, J1.pin6, J1.pin8, J1.pin10, J2.pin1, J2.pin3, J2.pin5, J2.pin7, J2.pin10, J3.pin3, J3.pin5, J3.pin10, J4.pin1, J4.pin4, J4.pin6, J4.pin8, J4.pin10, JOY.COM, S2_START.no_name_yet#2, S1_SEL.no_name_yet#2, L1.no_name_yet#2, R1.no_name_yet#2, L2.no_name_yet#2, R2.no_name_yet#2, OLED.GND, Fn.no_name_yet#1, NeoPixel_DIN.GND, B4.no_name_yet#1, B2.no_name_yet#1, B3.no_name_yet#1, B1.no_name_yet#1, A2.no_name_yet#1, A1_Home.no_name_yet#1, RESET.Pin_1, RESET.Pin_2, USB.pin4
  3.3V: KB2040.3.3V, J1.pin2, J2.pin9, OLED.VIN, NeoPixel_DIN.+5V
  N1: KB2040.SDA, OLED.MOSI_SDA
  N2: KB2040.SCL, OLED.SCLK_SCK
  N3: KB2040.D10, J4.pin7, R1.no_name_yet#1
  N4: KB2040.MOSI, J4.pin9, L1.no_name_yet#1
  N5: KB2040.MISO, J3.pin2, S1_SEL.no_name_yet#1
  N6: KB2040.SCLK, J3.pin4, S2_START.no_name_yet#1
  N7: KB2040.A0, J3.pin7, JOY.W
  N8: KB2040.A1, J3.pin9, JOY.N
  N9: KB2040.A2, J3.pin6, JOY.E
  N10: KB2040.A3, J3.pin8, JOY.S
  N11: KB2040.!RESET, J4.pin2, RESET.Pin_3, RESET.Pin_4
  N12: KB2040.RAW, USB.pin1
  N13: KB2040.D-, USB.pin3
  N14: KB2040.D+, USB.pin2
  N15: KB2040.D0, J1.pin3, A1_Home.no_name_yet#2
  N16: KB2040.D1, J1.pin5, A2.no_name_yet#2
  N17: KB2040.D2, J1.pin7, B2.no_name_yet#2
  N18: KB2040.D3, J1.pin9, B1.no_name_yet#2
  N19: KB2040.D4, J2.pin2, B4.no_name_yet#2
  N20: KB2040.D5, J2.pin4, B3.no_name_yet#2
  N21: KB2040.D6, J2.pin6, Fn.no_name_yet#2
  N22: KB2040.D7, J2.pin8, NeoPixel_DIN.DATAIN
  N23: KB2040.D8, J4.pin3, R2.no_name_yet#1
  N24: KB2040.D9, J4.pin5, L2.no_name_yet#1

notes:
  GND
  3V
  UP
  DN
  LF
  RT
  KB2040 Fightstick v1.0
  OLED
  John Park 2026
  D-
  D+
  VBUS
  S2 START
  S1 SEL
  L1
  R1
  L2
  R2
  RESET
  NeoPixel Din
  A1 Home
  Fn
  B3
  B4
  B1
  B2
  A2
  USB

custom parts:
  Arcade Button (yellow): Adafruit Arcade Button (yellow)
  Arcade Button (green): Adafruit Arcade Button (green)
  Arcade Button (blue): Adafruit Arcade Button (blue)
  OLED Monochrome 128x64 1.3 inch: These displays are small, only about 1.3" diagonal, but very readable due to the high contrast of an OLED display. This display is made of 128x64 individual white OLED pixels, each one is turned on or off by the controller chip. Because the display makes its own light, no backlight is required. This reduces the power required to run the OLED and is why the display has such high contrast; we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
  NeoPixel Stick: Make your own little LED strip arrangement with this stick of NeoPixel LEDs. We crammed 8 of the tiny 5050 (5mm x 5mm) smart RGB LEDs onto a PCB with mounting holes and a chainable design. Use only one microcontroller pin to control as many as you can chain together! Each LED is addressable as the driver chip is inside the LED. Each one has ~18mA constant current drive so the color will be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
  Arcade Button (red): Adafruit Arcade Button (red)
  Arcade Button (white): Adafruit Arcade Button (white)
